# Fritzing sketch anr2000 (saved by Fritzing 0.9.6b)
circuit board: 10cm x 5cm
breadboards: 3

parts:
  Componente3 = Arduino Nano (Rev3.0) (ICSP)
  U1 = 74HC595 [package="DIP16 [THT]"]
  R1 = Resistor [tolerance=±5% power=0.25 resistance=220 package=THT]
  R2 = Resistor [tolerance=±5% power=0.25 resistance=220 package=THT]
  R3 = Resistor [tolerance=±5% power=0.25 resistance=220 package=THT]
  R4 = Resistor [tolerance=±5% power=0.25 resistance=220 package=THT]
  R5 = Resistor [tolerance=±5% power=0.25 resistance=220 package=THT]
  R6 = Resistor [tolerance=±5% power=0.25 resistance=220 package=THT]
  R7 = Resistor [tolerance=±5% power=0.25 resistance=220 package=THT]
  R8 = Resistor [tolerance=±5% power=0.25 resistance=220 package=THT]
  R9 = Resistor [tolerance=±5% power=0.25 resistance=220 package=THT]
  J1 = female pin header, 9 pins [form="♀ (female)"]
  J2 = female pin header, 9 pins [form="♀ (female)"]
  R10 = Resistor [tolerance=±5% power=0.25 resistance=220 package=THT]
  R11 = Resistor [tolerance=±5% power=0.25 resistance=220 package=THT]
  R12 = Resistor [tolerance=±5% power=0.25 resistance=220 package=THT]
  R13 = Resistor [tolerance=±5% power=0.25 resistance=220 package=THT]
  R14 = Resistor [tolerance=±5% power=0.25 resistance=220 package=THT]
  R15 = Resistor [tolerance=±5% power=0.25 resistance=220 package=THT]
  R16 = Resistor [tolerance=±5% power=0.25 resistance=220 package=THT]
  R17 = Resistor [tolerance=±5% power=0.25 resistance=220 package=THT]
  R18 = Resistor [tolerance=±5% power=0.25 resistance=220 package=THT]
  J3 = female pin header, 2 pins [form="♀ (female)"]
  R19 = Resistor [tolerance=±5% power=0.25 resistance=220 package=THT]
  J4 = female pin header, 2 pins [form="♀ (female)"]

nets:
  GNC: Componente3.GND, U1.GND, J3.pin2, J4.pin1
  N1: Componente3.D2, U1.MR
  N2: Componente3.D3, U1.SH_CP
  N3: Componente3.D10, R18.Pin_1
  N4: Componente3.D11/MOSI, R17.Pin_1
  N5: Componente3.D12/MISO, R9.Pin_0
  N6: Componente3.VIN, J4.pin2
  5V: Componente3.5V, U1.VCC
  N7: Componente3.A7, R16.Pin_1
  N8: Componente3.A6, R10.Pin_1
  N9: Componente3.A5, R11.Pin_1
  N10: Componente3.A4, R12.Pin_1
  N11: Componente3.A3, R13.Pin_1
  N12: Componente3.A2, R14.Pin_1
  N13: Componente3.A1, R15.Pin_1
  N14: Componente3.D13/SCK, R19.Pin_0
  N15: U1.Q1, R1.Pin_0
  N16: U1.Q2, R2.Pin_0
  N17: U1.Q3, R3.Pin_0
  N18: U1.Q4, R4.Pin_0
  N19: U1.Q5, R5.Pin_0
  N20: U1.Q6, R6.Pin_0
  N21: U1.Q7, R7.Pin_0
  N22: U1.Q7', R8.Pin_0
  N23: R1.Pin_1, J1.pin8
  N24: R2.Pin_1, J1.pin7
  N25: R3.Pin_1, J1.pin6
  N26: R4.Pin_1, J1.pin5
  N27: R5.Pin_1, J1.pin4
  N28: R6.Pin_1, J1.pin3
  N29: R7.Pin_1, J1.pin2
  N30: R8.Pin_1, J1.pin1
  N31: R9.Pin_1, J1.pin9
  N32: J2.pin1, R18.Pin_0
  N33: J2.pin2, R17.Pin_0
  N34: J2.pin3, R15.Pin_0
  N35: J2.pin4, R14.Pin_0
  N36: J2.pin5, R13.Pin_0
  N37: J2.pin6, R12.Pin_0
  N38: J2.pin7, R11.Pin_0
  N39: J2.pin8, R10.Pin_0
  N40: J2.pin9, R16.Pin_0
  N41: J3.pin1, R19.Pin_1

notes:
  led encendido
  sensores touch
  leds
  12v
