# Fritzing sketch nr2000 (copia) (saved by Fritzing 0.9.6b)
circuit board: 10cm x 5cm
breadboards: 4

parts:
  U1 = 74HC595 [package="DIP16 [THT]"]
  R1 = Resistor [tolerance=±5% power=0.25 resistance=220 package=THT]
  R2 = Resistor [tolerance=±5% power=0.25 resistance=220 package=THT]
  R3 = Resistor [tolerance=±5% power=0.25 resistance=220 package=THT]
  R4 = Resistor [tolerance=±5% power=0.25 resistance=220 package=THT]
  R5 = Resistor [tolerance=±5% power=0.25 resistance=220 package=THT]
  R6 = Resistor [tolerance=±5% power=0.25 resistance=220 package=THT]
  R7 = Resistor [tolerance=±5% power=0.25 resistance=220 package=THT]
  R8 = Resistor [tolerance=±5% power=0.25 resistance=220 package=THT]
  R9 = Resistor [tolerance=±5% power=0.25 resistance=220 package=THT]
  R19 = Resistor [tolerance=±5% power=0.25 resistance=220 package=THT]
  J4 = female pin header, 2 pins [form="♀ (female)"]
  Componente3 = Arduino Nano (Rev3.0)
  J3 = female pin header, 2 pins [form="♀ (female)"]
  J1 = female pin header, 8 pins [form="♀ (female)"]
  J6 = female pin header, 8 pins [form="♀ (female)"]
  J9 = female pin header, 2 pins [form="♀ (female)"]
  J5 = female pin header, 10 pins [form="♀ (female)"]
  J10 = female pin header, 2 pins [form="♀ (female)"]
  R24 = Resistor [tolerance=±5% power=0.25 resistance=1M package=THT]
  R25 = Resistor [tolerance=±5% power=0.25 resistance=1M package=THT]
  R26 = Resistor [tolerance=±5% power=0.25 resistance=1M package=THT]
  R27 = Resistor [tolerance=±5% power=0.25 resistance=1M package=THT]
  R28 = Resistor [tolerance=±5% power=0.25 resistance=1M package=THT]
  R29 = Resistor [tolerance=±5% power=0.25 resistance=1M package=THT]
  R30 = Resistor [tolerance=±5% power=0.25 resistance=1M package=THT]
  R31 = Resistor [tolerance=±5% power=0.25 resistance=1M package=THT]
  R32 = Resistor [tolerance=±5% power=0.25 resistance=1M package=THT]
  R33 = Resistor [tolerance=±5% power=0.25 resistance=1M package=THT]
  R23 = Resistor [tolerance=±5% power=0.25 resistance=220 package=THT]

nets:
  N1: U1.Q1, R1.Pin_0
  N2: U1.Q2, R2.Pin_0
  N3: U1.Q3, R3.Pin_0
  N4: U1.Q4, R4.Pin_0
  N5: U1.Q5, R5.Pin_0
  N6: U1.Q6, R6.Pin_0
  N7: U1.Q7, R7.Pin_0
  gnd: U1.GND, U1.OE, J4.pin1, Componente3.GND, J3.pin2, J6.pin1, J6.pin2, J6.pin3, J6.pin4, J6.pin5, J6.pin6, J6.pin7, J6.pin8, J9.pin2, J10.pin1
  5V: U1.MR, U1.VCC, Componente3.5V
  pin 4: U1.SH_CP, Componente3.D4
  pin 3: U1.ST_CP, Componente3.D3
  pin 2: U1.DS, Componente3.D2
  N8: U1.Q0, R8.Pin_0
  N9: R1.Pin_1, J1.pin8
  N10: R2.Pin_1, J1.pin7
  N11: R3.Pin_1, J1.pin6
  N12: R4.Pin_1, J1.pin5
  N13: R5.Pin_1, J1.pin4
  N14: R6.Pin_1, J1.pin3
  N15: R7.Pin_1, J1.pin2
  N16: R8.Pin_1, J1.pin1
  pin 6: R9.Pin_0, Componente3.D6
  N17: R9.Pin_1, J9.pin1
  pin 7: R19.Pin_0, Componente3.D7
  N18: R19.Pin_1, J3.pin1
  vin: J4.pin2, Componente3.VIN
  pin 9: Componente3.D9, R24.Pin_0, R25.Pin_0, R26.Pin_0, R27.Pin_0, R28.Pin_0, R29.Pin_0, R30.Pin_0, R31.Pin_0, R32.Pin_0, R33.Pin_0
  pin 10: Componente3.D10, J5.pin3, R26.Pin_1
  pin 11: Componente3.D11/MOSI, J5.pin2, R25.Pin_1
  pin 12: Componente3.D12/MISO, J5.pin1, R24.Pin_1
  A 7: Componente3.A7, J5.pin10, R33.Pin_1
  A 6: Componente3.A6, J5.pin9, R32.Pin_1
  A 5: Componente3.A5, J5.pin8, R31.Pin_1
  A 4: Componente3.A4, J5.pin7, R30.Pin_1
  A 3: Componente3.A3, J5.pin6, R29.Pin_1
  A 2: Componente3.A2, J5.pin5, R28.Pin_1
  A 1: Componente3.A1, J5.pin4, R27.Pin_1
  N19: Componente3.D13/SCK, R23.Pin_1
  N20: J10.pin2, R23.Pin_0

notes:
  sensores touch
  leds
  12v
  neuro reabilitador 0.01v
  neuro reabilitador, 0.01
