# Fritzing sketch nr2000 (saved by Fritzing 0.9.6b)
circuit board: 10cm x 5cm
breadboards: 4

parts:
  U1 = 74HC595 [package="DIP16 [THT]"]
  R1 = Resistor [tolerance=±5% power=0.25 resistance=220 package=THT]
  R2 = Resistor [tolerance=±5% power=0.25 resistance=220 package=THT]
  R3 = Resistor [tolerance=±5% power=0.25 resistance=220 package=THT]
  R4 = Resistor [tolerance=±5% power=0.25 resistance=220 package=THT]
  R5 = Resistor [tolerance=±5% power=0.25 resistance=220 package=THT]
  R6 = Resistor [tolerance=±5% power=0.25 resistance=220 package=THT]
  R7 = Resistor [tolerance=±5% power=0.25 resistance=220 package=THT]
  R8 = Resistor [tolerance=±5% power=0.25 resistance=220 package=THT]
  R9 = Resistor [tolerance=±5% power=0.25 resistance=220 package=THT]
  R19 = Resistor [tolerance=±5% power=0.25 resistance=220 package=THT]
  J4 = female pin header, 2 pins [form="♀ (female)"]
  Componente3 = Arduino Nano (Rev3.0)
  J3 = female pin header, 2 pins [form="♀ (female)"]
  J1 = female pin header, 8 pins [form="♀ (female)"]
  J6 = female pin header, 8 pins [form="♀ (female)"]
  R22 = Resistor [tolerance=±5% power=0.25 resistance=1M package=THT]
  J9 = female pin header, 2 pins [form="♀ (female)"]
  J5 = female pin header, 10 pins [form="♀ (female)"]
  R23 = Resistor [tolerance=±5% power=0.25 resistance=220 package=THT]
  J10 = female pin header, 2 pins [form="♀ (female)"]

nets:
  N1: U1.Q1, R1.Pin_0
  N2: U1.Q2, R2.Pin_0
  N3: U1.Q3, R3.Pin_0
  N4: U1.Q4, R4.Pin_0
  N5: U1.Q5, R5.Pin_0
  N6: U1.Q6, R6.Pin_0
  N7: U1.Q7, R7.Pin_0
  gnd: U1.GND, U1.OE, J4.pin1, Componente3.GND, J3.pin2, J6.pin1, J6.pin2, J6.pin3, J6.pin4, J6.pin5, J6.pin6, J6.pin7, J6.pin8, J9.pin2, J10.pin1
  5V: U1.MR, U1.VCC, Componente3.5V
  pin 4: U1.SH_CP, Componente3.D4
  pin 3: U1.ST_CP, Componente3.D3
  pin 2: U1.DS, Componente3.D2
  N8: U1.Q0, R8.Pin_0
  N9: R1.Pin_1, J1.pin8
  N10: R2.Pin_1, J1.pin7
  N11: R3.Pin_1, J1.pin6
  N12: R4.Pin_1, J1.pin5
  N13: R5.Pin_1, J1.pin4
  N14: R6.Pin_1, J1.pin3
  N15: R7.Pin_1, J1.pin2
  N16: R8.Pin_1, J1.pin1
  pin 6: R9.Pin_0, Componente3.D6
  N17: R9.Pin_1, J9.pin1
  pin 7: R19.Pin_0, Componente3.D7
  N18: R19.Pin_1, J3.pin1
  vin: J4.pin2, Componente3.VIN
  pin 9: Componente3.D9, R22.Pin_1
  A 1/A 2/A 3/A 4/A 5/A 6/A 7/pin 10/pin 11/pin 12: Componente3.D10, Componente3.D11/MOSI, Componente3.D12/MISO, Componente3.A7, Componente3.A6, Componente3.A5, Componente3.A4, Componente3.A3, Componente3.A2, Componente3.A1, R22.Pin_0, J5.pin1, J5.pin2, J5.pin3, J5.pin4, J5.pin5, J5.pin6, J5.pin7, J5.pin8, J5.pin9, J5.pin10
  N19: Componente3.D13/SCK, R23.Pin_1
  N20: R23.Pin_0, J10.pin2

notes:
  sensores touch
  leds
  12v
  neuro reabilitador 0.01v
  neuro reabilitador, 0.01

// code stored in the sketch: nr2000.ino
/*
  Autor: fedemos
  licencia: gpl3
  fecha: 7/11/2021
  versión: 0.0.2
*/

int pinData  = 2;
int pinLatch = 3;
int pinClock = 4;
int contador = 1;
int milistaLed[] = {B00000001, B00000010, B00000100, B00001000, B00010000, B00100000, B01000000, B1000000, 12 };
long randomNumber;
/* 
https://github.com/PaulStoffregen/CapacitiveSensor
https://www.arduino.cc/reference/en/libraries/capacitivesensor/
*/
// libreria para sensor capasitivo
#include <CapacitiveSensor.h>
CapacitiveSensor   sensor1 = CapacitiveSensor(5, 6);
CapacitiveSensor   sensor2 = CapacitiveSensor(5, 7);
CapacitiveSensor   sensor3 = CapacitiveSensor(5, A1);
CapacitiveSensor   sensor4 = CapacitiveSensor(5, A2);
CapacitiveSensor   sensor5 = CapacitiveSensor(5, A3);
CapacitiveSensor   sensor6 = CapacitiveSensor(5, A4);
CapacitiveSensor   sensor7 = CapacitiveSensor(5, A5);
CapacitiveSensor   sensor8 = CapacitiveSensor(5, A6);
CapacitiveSensor   sensor9 = CapacitiveSensor(5, A7);
CapacitiveSensor   sensor10 = CapacitiveSensor(5, 8);

/*
    --------------------------------------
    prende el Led aleatoreo
   --------------------------------------
*/

void ledWrite(int Led) {
  if (milistaLed[randomNumber] == 8) {
    digitalWrite(12, HIGH);
  }
  else {
    digitalWrite(pinLatch, LOW);
    shiftOut(pinData, pinClock, LSBFIRST, Led);
    digitalWrite(pinLatch, HIGH);
  }

}

/*
    -----------------------------------------
    tiempo de tiempo entre que se presiona el
    sensor capasitivo y se prende el póxmo LED
    ------------------------------------------
*/

int espera(int x) {
  // si el x es menor a 8 el tiempo es de 1000ms
  if (x < 8) {
    return 1000;
  }
  // si el x es igual a 8 o menor a 16 el tiempo es de 500ms
  else if (x = 8 or x < 16) {
    return 500;
  }
  // si el x es igual a 16 o menor a 24 el tiempo es de 250ms
  else if (x = 16 or x < 24) {
    return 250;
  }
  // si el x es igual a 24 o menor a 32 el tiempo es de 100ms
  else if (x = 24 or x < 32) {
    return 100;
  }
  // si no se dan las otras hipótesis el tiempo es de 50ms
  else  {
    return 50;
  }
}

// ----------------------------------

void setup() {
  Serial.begin(9600);
  Serial.println("Autor: fedemos");
  Serial.println("licencia: gpl3 ");
  Serial.println("fecha: 7/11/2021");
  Serial.println("versión: 0.0.2");

  // los pines para controlar el 74hc595
  pinMode(pinData, OUTPUT);
  pinMode(pinLatch, OUTPUT);
  pinMode(pinClock, OUTPUT);

  //declara el pin 12 como salida
  pinMode(12, OUTPUT);

  //declara el pin 13 como salida
  pinMode(13, OUTPUT);

  // apaga todos los led
  shiftOut(pinData, pinClock, LSBFIRST, B00000000);

  //para hacer que el random sea seudo aleatorio
  randomSeed(analogRead(A0));

  //enciende el pin 13
  digitalWrite(13, HIGH);

}

/*
  ---------------------------
  función random
  ---------------------------
*/

void aleatorio(int x) {

  // da un número del 0 al 8
  randomNumber = random(0, 8);

  //tiempo de espera antes de hacer el random
  delay(x);

  // prende el led
  ledWrite(milistaLed[randomNumber]);

  //luego de hacer el random le suma 1 al contador
  contador++;
}

/*
   ---------------
   inicio del cilo
   ---------------
*/

void ciclo() {
  // cuando se cumple el tiempo termina el ciclo
  tiempo();
  long programa1 =  sensor2.capacitiveSensor(30);//5,7
  long programa2 =  sensor3.capacitiveSensor(30);//5,A1
  long programa3 =  sensor4.capacitiveSensor(30);//5,A2
  long programa4 =  sensor5.capacitiveSensor(30);//5,A3
  long programa5 =  sensor6.capacitiveSensor(30);//5,A4
  long programa6 =  sensor7.capacitiveSensor(30);//5,A5
  long programa7 =  sensor8.capacitiveSensor(30);//5,A6
  long programa8 =  sensor9.capacitiveSensor(30);//5,A7
  long programa9 =  sensor10.capacitiveSensor(30);//5,8


  if ((programa1 > 50 ) && (randomNumber == 0)) {
    shiftOut(pinData, pinClock, LSBFIRST, B00000000);
    aleatorio(espera(contador));
  }
  if ((programa2 > 50 ) && (randomNumber == 1)) {
    shiftOut(pinData, pinClock, LSBFIRST, B00000000);
    aleatorio(espera(contador));
  }
  if ((programa3 > 50 ) && (randomNumber == 2)) {
    shiftOut(pinData, pinClock, LSBFIRST, B00000000);
    aleatorio(espera(contador));
  }
  if ((programa4 > 50 ) && (randomNumber == 3)) {
    shiftOut(pinData, pinClock, LSBFIRST, B00000000);
    aleatorio(espera(contador));
  }
  if ((programa5 > 50 ) && (randomNumber == 4)) {
    shiftOut(pinData, pinClock, LSBFIRST, B00000000);
    aleatorio(espera(contador));
  }
  if ((programa6 > 50 ) && (randomNumber == 5)) {
    shiftOut(pinData, pinClock, LSBFIRST, B00000000);
    aleatorio(espera(contador));
  }
  if ((programa7 > 50 ) && (randomNumber == 6)) {
    shiftOut(pinData, pinClock, LSBFIRST, B00000000);
    aleatorio(espera(contador));
  }
  if ((programa8 > 50 ) && (randomNumber == 7)) {
    shiftOut(pinData, pinClock, LSBFIRST, B00000000);
    aleatorio(espera(contador));
  }
  if ((programa9 > 50 ) && (randomNumber == 8)) {
    digitalWrite(12, LOW);
    aleatorio(espera(contador));
  }


}

/*
   -----------------
   inicio de ciclo
   -----------------
*/

void iniciarCiclo() {
  long inicio =  sensor1.capacitiveSensor(30);
  //si se toca el sensor
  if (inicio > 50) {
    //prende el LED del pin 12
    //digitalWrite(12, HIGH);
    // imprime inicio en el puerto de serie
    Serial.println("inicio ");
    //espera 1000ms
    delay(1000);
    // hace el primer random
    ledWrite(milistaLed[randomNumber]);
    //inicia la fuciión ciclo
    ciclo;
  }
}

/*
   ---------------------------------
   tiempo en que se ejecuta el ciclo
   ---------------------------------
*/

void tiempo() {
  unsigned long tiempos = millis();
  unsigned long intervalo = 60000; // 1 minuto
  unsigned long ahora = millis();
  if (ahora - tiempos >= intervalo) { //si se cumple 1 minuto
    tiempos = ahora;
    for (int i = 0; i <= 3; i++) {
      // prende todos los led
      shiftOut(pinData, pinClock, LSBFIRST, B11111111);
    }
    delay(1000); //espera 1000ms
    for (int i = 0; i <= 3; i++) {
      // apaga todos los led
      shiftOut(pinData, pinClock, LSBFIRST, B00000000);
      //apaga el LED de inicio
      digitalWrite(12, LOW);
      // imprime fin de ciclo en el puerto de serie
      Serial.println("fin de ciclo");
    }
    //espera 1500ms
    delay(1500);
    // pone el contador en 1
    contador = 1;
    // vuelve a loop()
    loop;
  }
}
void loop() {
  iniciarCiclo();

}
